// Logisim project 6551071028_LAB1_2.circ as structural Verilog: 1 circuit, main circuit main
module main (
  input  A,
  input  B,
  input  A_2,
  output Y
);

  wire and_1_out;

  and and_1 (and_1_out, A, B);
  xor xor_1 (Y, and_1_out, A_2);
endmodule
