// Logisim project 6551071028_LAB1_3.circ as structural Verilog: 1 circuit, main circuit main
module main (
  input  B3,
  input  A3,
  input  B2,
  input  A2,
  input  B1,
  input  A1,
  input  B0,
  input  A0,
  input  in_9,
  output out_10,
  output S3,
  output S2,
  output S1,
  output S0
);

  wire and_1_out, and_2_out, and_3_out, and_4_out, and_5_out, and_6_out, and_7_out, and_8_out, or_2_out,
       or_3_out, or_4_out, xor_1_out, xor_3_out, xor_5_out, xor_7_out;

  or or_1 (out_10, and_1_out, and_2_out);
  and and_1 (and_1_out, A3, A3);
  xor xor_1 (xor_1_out, A3, A3);
  and and_2 (and_2_out, xor_1_out, or_2_out);
  or or_2 (or_2_out, and_3_out, and_4_out);
  xor xor_2 (S3, xor_1_out, or_2_out);
  and and_3 (and_3_out, A2, A2);
  xor xor_3 (xor_3_out, A2, A2);
  and and_4 (and_4_out, xor_3_out, or_3_out);
  xor xor_4 (S2, xor_3_out, or_3_out);
  or or_3 (or_3_out, and_5_out, and_6_out);
  and and_5 (and_5_out, B1, A1);
  and and_6 (and_6_out, xor_5_out, or_4_out);
  xor xor_5 (xor_5_out, B1, A1);
  xor xor_6 (S1, xor_5_out, or_4_out);
  or or_4 (or_4_out, and_7_out, and_8_out);
  and and_7 (and_7_out, B0, A0);
  and and_8 (and_8_out, xor_7_out, in_9);
  xor xor_7 (xor_7_out, B0, A0);
  xor xor_8 (S0, xor_7_out, in_9);

  assign B2 = A2;
  assign B3 = A3;
endmodule
