// Logisim project 6551071028_LAB1_4.circ as structural Verilog: 1 circuit, main circuit main
module main (
  input  B1,
  input  B0,
  input  B1_2,
  input  A1,
  input  B0_2,
  input  A0,
  input  A3,
  input  A2,
  input  in_9,
  output out_10,
  output S3,
  output S2,
  output S1,
  output S0
);

  wire and_1_out, and_2_out, and_3_out, and_4_out, and_5_out, and_6_out, and_7_out, and_8_out, and_10_out,
       and_11_out, not_1_out, not_2_out, not_3_out, not_4_out, or_2_out, or_3_out, or_4_out, xor_2_out,
       xor_5_out, xor_7_out, xor_8_out, xor_10_out, xor_11_out;

  or or_1 (out_10, and_1_out, and_2_out);
  and and_1 (and_1_out, A3, A3);
  not not_1 (not_1_out, B1);
  xor xor_1 (A3, and_3_out, not_1_out);
  xor xor_2 (xor_2_out, A3, A3);
  and and_2 (and_2_out, xor_2_out, or_2_out);
  or or_2 (or_2_out, and_4_out, and_5_out);
  xor xor_3 (S3, xor_2_out, or_2_out);
  and and_3 (and_3_out, and_6_out, not_2_out);
  and and_4 (and_4_out, A2, A2);
  not not_2 (not_2_out, B0);
  xor xor_4 (A2, and_6_out, not_2_out);
  xor xor_5 (xor_5_out, A2, A2);
  and and_5 (and_5_out, xor_5_out, or_3_out);
  xor xor_6 (S2, xor_5_out, or_3_out);
  or or_3 (or_3_out, and_7_out, and_8_out);
  and and_6 (and_6_out, not_3_out, not_3_out);
  and and_7 (and_7_out, xor_7_out, A1);
  and and_8 (and_8_out, xor_8_out, or_4_out);
  not not_3 (not_3_out, B1_2);
  xor xor_7 (xor_7_out, not_3_out, not_3_out);
  xor xor_8 (xor_8_out, xor_7_out, A1);
  xor xor_9 (S1, xor_8_out, or_4_out);
  or or_4 (or_4_out, and_10_out, and_11_out);
  and and_9 (not_3_out, 1'b1, not_4_out);
  and and_10 (and_10_out, xor_10_out, A0);
  and and_11 (and_11_out, xor_11_out, in_9);
  not not_4 (not_4_out, B0_2);
  xor xor_10 (xor_10_out, 1'b1, not_4_out);
  xor xor_11 (xor_11_out, xor_10_out, A0);
  xor xor_12 (S0, xor_11_out, in_9);
endmodule
